# Fritzing sketch Sketsa Gambaran (saved by Fritzing 0.9.3b)
breadboards: 1

parts:
  Part1 = Arduino Uno (Rev3)
  J1 = Piezo Speaker
  LED1 = LED - 5mm [color="Red (633nm)" package="5 mm [THT]"]
  hc-sr1 = hc-sr04
  J2 = Basic Servo
  R2 = Resistor [tolerance=±5% resistance=220 package="0402 [SMD]"]
  LED2 = LED - 5mm [color="Red (633nm)" package="5 mm [THT]"]
  R3 = Resistor [tolerance=±5% resistance=220 package="0402 [SMD]"]

nets:
  N1: Part1.D8, hc-sr1.Trig
  N2: Part1.D9_PWM, hc-sr1.Echo
  N3: Part1.D10_PWM/SS, J2.pulse
  N4: Part1.D11_PWM/MOSI, J1.pin2
  N5: Part1.D12/MISO, R3.Pin_1
  N6: Part1.D13/SCK, R2.Pin_1
  VCC: Part1.5V, hc-sr1.VCC, J2.vcc
  GND: Part1.GND, J1.pin1, LED1.cathode, hc-sr1.GND, J2.gnd, LED2.cathode
